// Logisim project lab0_1.circ as structural Verilog: 1 circuit, main circuit main
module main (
  input  I0,
  input  I1,
  input  I2,
  output O
);

  wire and_1_out, and_2_out, and_3_out, and_4_out, not_1_out, not_2_out, not_3_out;

  not not_1 (not_1_out, I0);
  not not_2 (not_2_out, I1);
  not not_3 (not_3_out, I2);
  and and_1 (and_1_out, I0, not_2_out, not_3_out);
  and and_2 (and_2_out, not_1_out, I1, not_3_out);
  and and_3 (and_3_out, not_1_out, not_2_out, I2);
  and and_4 (and_4_out, I0, I1, I2);
  or or_1 (O, and_1_out, and_2_out, and_3_out, and_4_out);
endmodule
